# Fritzing sketch Babalola_Amen (saved by Fritzing 0.9.3b)

parts:
  ARDUINO_NANO = Arduino Nano (Rev3.0)
  5V_BOOST_CONVERTER = PowerBoost 500 Charger
  VCC1 = Battery
  R1 = PHOTOCELL [package=photocell-kit]
  IRF3205_MOSFET = Basic FET N-Channel [package="DPak [SMD]"]
  R2 = Trimmer Potentiometer [maximum_resistance=10kΩ package=THT]
  3_7V_CHARGING_CIRCUIT = TP4056 [chip_label=TP4056 package="DIP (Dual Inline) [THT]"]
  JACK_TERMINAL = 2.1mm Barrel Jack with Terminal Block
  BUCK_CONVERTER = Oiysgsi buck regulator 3A Dual usb output
  R4 = Resistor [tolerance=±5% resistance=10k package=THT]
  R5 = Resistor [tolerance=±5% resistance=10k package=THT]
  R6 = Resistor [tolerance=±5% resistance=220 package=THT]
  R7 = Resistor [tolerance=±5% resistance=100k package=THT]
  LED_LAMP = MAX7219 8x8 single Led Matrix Module
  BATTERY_LEVEL_LEDS = LED - 5mm [color="Red (633nm)" package="5 mm [THT]"]
  LED2 = LED - 5mm [color="Red (633nm)" package="5 mm [THT]"]
  LED3 = LED - 5mm [color="Red (633nm)" package="5 mm [THT]"]
  LED4 = LED - 5mm [color="Red (633nm)" package="5 mm [THT]"]
  R8 = Resistor [tolerance=±5% resistance=220 package=THT]
  R9 = Resistor [tolerance=±5% resistance=220 package=THT]
  R10 = Resistor [tolerance=±5% resistance=220 package=THT]
  R11 = Resistor [tolerance=±5% resistance=220 package=THT]
  12V_SOLAR_PANEL = Solar Panel [package="Renogy 50 Watts 12 Volt Monocrystalline Bendable Solar Panel"]

nets:
  GND: ARDUINO_NANO.GND, 5V_BOOST_CONVERTER.GND, R1.P$2, IRF3205_MOSFET.source, R2.leg1, R2.wiper, R7.Pin_1, BATTERY_LEVEL_LEDS.cathode, LED2.cathode, LED3.cathode, LED4.cathode
  N1: ARDUINO_NANO.D3, R11.Pin_0
  N2: ARDUINO_NANO.D4, R10.Pin_0
  N3: ARDUINO_NANO.D5, R9.Pin_0
  N4: ARDUINO_NANO.D6, R8.Pin_0
  N5: ARDUINO_NANO.D9, R6.Pin_0
  N6: ARDUINO_NANO.5V, 5V_BOOST_CONVERTER.5.0V, R5.Pin_0, LED_LAMP.I-VCC-1, LED_LAMP.O-VCC-1, LED_LAMP.I-VCC-2, LED_LAMP.O-VCC-2, LED_LAMP.I-VCC-3, LED_LAMP.O-VCC-3, LED_LAMP.I-VCC-4
  N7: ARDUINO_NANO.A1, R1.P$1, R5.Pin_1
  N8: ARDUINO_NANO.A0, R2.leg2, R4.Pin_1
  N9: 5V_BOOST_CONVERTER.GND_BAT_IN, VCC1.+, 3_7V_CHARGING_CIRCUIT.pin5
  N10: 5V_BOOST_CONVERTER.VBAT_IN, VCC1.-, 3_7V_CHARGING_CIRCUIT.pin4, R4.Pin_0
  N11: IRF3205_MOSFET.Gate, R6.Pin_1, R7.Pin_0
  N12: IRF3205_MOSFET.drain, LED_LAMP.I-GND-1, LED_LAMP.O-GND-1, LED_LAMP.I-GND-2, LED_LAMP.O-GND-2, LED_LAMP.I-GND-3, LED_LAMP.O-GND-3, LED_LAMP.I-GND-4, LED_LAMP.O-GND-4
  N13: 3_7V_CHARGING_CIRCUIT.pin1, BUCK_CONVERTER.Pin_5
  N14: 3_7V_CHARGING_CIRCUIT.pin2, BUCK_CONVERTER.Pin_6
  N15: JACK_TERMINAL.POS, BUCK_CONVERTER.Pin_2, 12V_SOLAR_PANEL.Connector_1
  N16: JACK_TERMINAL.NEG, BUCK_CONVERTER.Pin_1, 12V_SOLAR_PANEL.Connector_2
  N17: BATTERY_LEVEL_LEDS.anode, R11.Pin_1
  N18: LED2.anode, R8.Pin_1
  N19: LED3.anode, R10.Pin_1
  N20: LED4.anode, R9.Pin_1

custom parts:
  Battery: Your standard 2x 18650 battery pack (14.7 Volts)
  TP4056: A DIP stand-in part for whatever IC you want. With 6 pins on a 300mil dual inline package (DIP) footprint.
  Oiysgsi buck regulator 3A Dual usb output: Oiysgsi buck regulator 3A Dual usb output.
  MAX7219 8x8 single Led Matrix Module: Description: MAX7219 8x8 LedMatrix single Red Module Dimensions: 32x32mm Documents:
  Solar Panel: Renogy 50 Watts 12 Volt Solar Panel
