# Fritzing sketch ClimateMonitoring (saved by Fritzing 0.9.3b)

parts:
  5V_Boost_Converter = PowerBoost 500 Charger
  DS3231_RTC = ZS-042 RTC Module
  microSD = MicroSD Card Module
  DHT22 = DHT22 Humidity and Temperature Sensor
  Capacitive_Soil_Moisture = DFRobot Capacitive Soil Moisture Sensor V1.0 [part_number=SEN0193]
  LDR = Photocell (LDR) [package=THT]
  Solar_Panel = Solar Panel [package="Renogy 50 Watts 12 Volt Monocrystalline Bendable Solar Panel"]
  ESP32 = ESP32-38PinWide [part_number=ESP32-38PinWide]
  3_7V_Li-ion = Battery
  R2 = Resistor [tolerance=±5% resistance=10k package=THT]
  Buck_Converter = Buck Convertor [part_number=LM2596 package=THT]
  R3 = Resistor [tolerance=±5% resistance=10k package=THT]

nets:
  N1: 5V_Boost_Converter.GND_BAT_IN, 3_7V_Li-ion.-, Buck_Converter.Negative_Output
  N2: 5V_Boost_Converter.VBAT_IN, 3_7V_Li-ion.+, Buck_Converter.Positive_Output
  GND: 5V_Boost_Converter.GND, DS3231_RTC.GND, microSD.GND, DHT22.GND, Capacitive_Soil_Moisture.GND, ESP32.GND, R2.Pin_1
  VCC: 5V_Boost_Converter.5.0V, DS3231_RTC.VCC, microSD.VCC, DHT22.VDD, Capacitive_Soil_Moisture.VCC, LDR.pin_0, ESP32.VIN, R3.Pin_0
  N3: DS3231_RTC.SDA, ESP32.GPIO21
  N4: DS3231_RTC.SCL, ESP32.GPIO22
  N5: microSD.MISO, ESP32.GPIO19
  N6: microSD.MOSI, ESP32.GPIO23
  N7: microSD.SCK, ESP32.GPIO18
  N8: microSD.CS, ESP32.GPIO5
  N9: DHT22.DATA, ESP32.GPIO4, R3.Pin_1
  N10: Capacitive_Soil_Moisture.A, ESP32.GPIO35
  N11: LDR.pin_1, ESP32.GPIO34, R2.Pin_0
  N12: Solar_Panel.Connector_1, Buck_Converter.Positive_Input
  N13: Solar_Panel.Connector_2, Buck_Converter.Negative_Input

custom parts:
  DFRobot Capacitive Soil Moisture Sensor V1.0: DFRobot Capacitive Soil Moisture Sensor V1.0 This product measures soil moisture levels by capacitive sensing, rather than resistive sensing like other types of moisture sensor. It is made of a corrosion resistant material giving it a long service life. Insert it into soil and impress your friends with the real-time soil moisture data! The product includes an on-board voltage regulator which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
  Solar Panel: Renogy 50 Watts 12 Volt Solar Panel
  ESP32-38PinWide: Generic 38-Pin ESP32 with wide format (only access to one side of pins on a breadboard) based on Stephen Lilley's HiLetgo ESP-WROOM-32 ESP32 ESP-32S Development Board.
  Battery: Your standard 2x 18650 battery pack (14.7 Volts)
  Buck Convertor: DC to DC buck convertor
