# Fritzing sketch M-CanSat (saved by Fritzing 0.9.3b)
circuit board: 11.0647cm x 6.62681cm

parts:
  Pico/Pico2_Mod_1 = Raspberry Pi Pico or Pico 2
  C1 = Electrolytic Capacitor [capacitance=10µF voltage=10V package="0405 [SMD, electrolytic]"]
  MT3608 = MT3608 Boost No usb
  BME280 = female pin header, 4 pins [form="♀ (female)"]
  MQ7 = female pin header, 4 pins [form="♀ (female)"]
  NRF_R2 = female pin header, 4 pins [form="♀ (female)"]
  NRF_R1 = female pin header, 4 pins [form="♀ (female)"]
  SERVO = female pin header, 3 pins [form="♀ (female)"]

nets:
  N1: Pico/Pico2_Mod_1.pin_3, Pico/Pico2_Mod_1.pin_13, Pico/Pico2_Mod_1.pin_33, Pico/Pico2_Mod_1.pin_38, Pico/Pico2_Mod_1.pin_42, C1.-, MT3608.OUT_(-), BME280.pin2, MQ7.pin2, NRF_R2.pin4, SERVO.pin3
  N2: Pico/Pico2_Mod_1.pin_6, NRF_R2.pin1
  N3: Pico/Pico2_Mod_1.pin_9, NRF_R2.pin2
  N4: Pico/Pico2_Mod_1.pin_10, NRF_R1.pin2
  N5: Pico/Pico2_Mod_1.pin_19, NRF_R2.pin3
  N6: Pico/Pico2_Mod_1.pin_20, NRF_R1.pin3
  N7: Pico/Pico2_Mod_1.pin_24, SERVO.pin1
  N8: Pico/Pico2_Mod_1.pin_26, BME280.pin4
  N9: Pico/Pico2_Mod_1.pin_27, BME280.pin3
  N10: Pico/Pico2_Mod_1.pin_31, MQ7.pin4
  N11: Pico/Pico2_Mod_1.pin_36, C1.+, BME280.pin1, NRF_R1.pin4
  N12: Pico/Pico2_Mod_1.pin_39, MT3608.OUT_(+), SERVO.pin2

custom parts:
  Raspberry Pi Pico or Pico 2: Raspberry Pi Pico and Pico 2. Based around the RP2040 and RP2350 microcontrollers respectively, Picos are low cost microcontroller device bringing Raspberry Pi quality, cost, and easy of use to the microcontroller space. Jan 2021, Split part in to two versions: tht (this one) and SMD. This one will drill holes for a .1 in header in pcb to allow plugging in the module as well as providing pads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
  MT3608 Boost No usb: Chip- MT3608 / B6289 DC to DC step up, power booster module. With adjustable output voltage. Current- 2A . || Input voltage- 2V-24V || Output voltage- 5V-28V Input interface- Inversed polarity- NO. || Led indicator- No.
