# Fritzing sketch M_schm (saved by Fritzing 0.9.3b)

parts:
  U1 = ESP32-38PinWide [part_number=ESP32-38PinWide]
  LCD = LCD1602-I2C
  3_7V_-_5V_DC_Converter = PowerBoost 500 Charger
  Buzzer = Piezo Speaker
  R1 = Resistor [tolerance=±5% resistance=220 package="2010 [SMD]"]
  J2 = Camdenboss CTB0158-2 [part_number="Chrager Input" package=THT]
  Bat1 = battery_holder_dual_18650 [part_number=TBH-18650-2A-P]
  BC547 = TRANSISTOR_NPN [package=to-92]
  MQ7 = MQ-7 breakout
  3_7v_Lithium_Charger = Power Cell LiPo Charger/Booster

nets:
  N1: U1.GPIO35, MQ7.AO
  GND: U1.GND, LCD.GND, 3_7V_-_5V_DC_Converter.GND, BC547.E, MQ7.GND
  VCC: U1.VIN, LCD.VCC, 3_7V_-_5V_DC_Converter.5.0V, Buzzer.pin1, MQ7.VCC
  N2: U1.GPIO16, R1.Pin_0
  N3: U1.GPIO21, LCD.SDA
  N4: U1.GPIO22, LCD.SCL
  N5: 3_7V_-_5V_DC_Converter.GND_BAT_IN, J2.pin2, Bat1.+#2, Bat1.+#3, 3_7v_Lithium_Charger.GND
  N6: 3_7V_-_5V_DC_Converter.VBAT_IN, Bat1.+#0, Bat1.+#1, 3_7v_Lithium_Charger.VBATT
  N7: Buzzer.pin2, BC547.C
  N8: R1.Pin_1, BC547.B
  N9: J2.pin1, 3_7v_Lithium_Charger.5VIN

custom parts:
  ESP32-38PinWide: Generic 38-Pin ESP32 with wide format (only access to one side of pins on a breadboard) based on Stephen Lilley's HiLetgo ESP-WROOM-32 ESP32 ESP-32S Development Board.
  LCD1602-I2C: A standard character display, usually with 2x16 characters. Comes in many colors with LCM1602 IIC attached.
  battery_holder_dual_18650: TBH-18650-2A-P dual 18650 battery holder.
  MQ-7 breakout: SKU: 101282
