# Fritzing sketch MedShield Circuit (saved by Fritzing 0.9.3b)
circuit board: 4.41092cm x 5.06484cm

parts:
  R2 = TRIMPOT [package=trim_pot_pth]
  J1 = Piezo Speaker
  + = Camdenboss CTB0158-2 [part_number=CTB0158-2 package=THT]
  U1 = 555 Timer [package="DIP8 [THT]"]
  R1 = Resistor [tolerance=±5% resistance=3.3k package=THT]
  C2 = Ceramic Capacitor [capacitance=10nF voltage=16V package="200 mil [THT, multilayer]"]
  R3 = Resistor [tolerance=±10% resistance=220 package=THT]
  C1 = Ceramic Capacitor [capacitance=10nF voltage=16V package="200 mil [THT, multilayer]"]
  Q1 = NPN-Transistor [package="TO92 [THT]"]
  U2 = ESP32-38PinWide [part_number=ESP32-38PinWide]
  DS1 = DS18B20 1-Wire Temperature Sensor Probe
  R4 = Resistor [tolerance=±5% resistance=4.7k package=THT]
  M1 = MakerFocus MAX30102
  Part1 = LCD1602-I2C

nets:
  N1: R2.WIPER, U1.Trigger, U1.Threshold, C1.1
  N2: R2.CW, U1.Discharge, R1.Pin_1
  N3: J1.pin1, +.pin1, U1.Reset, U1.Vcc_Supply_Voltage, R1.Pin_0
  N4: J1.pin2, Q1.C
  GND: +.pin2, C1.0, U2.GND, DS1.GND, M1.GND, Part1.GND
  VIN: +.terminal_1, U2.VIN, M1.VIN, Part1.VCC
  N5: U1.Output, R3.Pin_0
  N6: U1.Control_Voltage, C2.1
  N7: C2.0, Q1.E
  N8: R3.Pin_1, Q1.B
  N9: U2.3.3, DS1.VDD, R4.Pin_0
  N10: U2.GPIO4, DS1.DQ, R4.Pin_1
  N11: U2.GPIO21, M1.SDA, Part1.SDA
  N12: U2.GPIO22, M1.SCL, Part1.SCL

notes:
  Mosquito Repellent Circuit

custom parts:
  ESP32-38PinWide: Generic 38-Pin ESP32 with wide format (only access to one side of pins on a breadboard) based on Stephen Lilley's HiLetgo ESP-WROOM-32 ESP32 ESP-32S Development Board.
  MakerFocus MAX30102: Oximeter module using the MAX30102 chip. As usual, if you want the mounting holes in pcb, you need to drag a hole over the pad in silkscreen to actually drill the hole (by default they are not drilled)
  LCD1602-I2C: A standard character display, usually with 2x16 characters. Comes in many colors with LCM1602 IIC attached.
