# Fritzing sketch Taiwo (saved by Fritzing 0.9.3b)

parts:
  U1 = ESP32-38PinWide [part_number=ESP32-38PinWide]
  LCD = LCD1602-I2C
  Soil_Moisture = Soil Moisture Sensor
  5V_Relay = 1 chan 5v relay module
  DHT11 = Humidity and Temperature Sensor DHT11
  +5V_Power_Supply = Camdenboss CTB0158-2 [part_number=CTB0158-2 package=THT]
  Water/Rain_Sensor1 = Water Level Sensor
  Water_Pump = DC Motor
  Switch = Square Pushbutton

nets:
  N1: U1.GPIO34, Water/Rain_Sensor1.SIG
  N2: U1.GPIO35, Soil_Moisture.SIG
  GND: U1.GND, LCD.GND, Soil_Moisture.GND, 5V_Relay.pin_2, DHT11.GND_2, +5V_Power_Supply.pin2, Water/Rain_Sensor1.GND, Water_Pump.pin_2
  5V: U1.VIN, LCD.VCC, Soil_Moisture.VCC, 5V_Relay.pin_1, 5V_Relay.pin_5, DHT11.Vcc, Water/Rain_Sensor1.VCC, Switch.leg0
  N3: U1.GPIO4, DHT11.Data-signal
  N4: U1.GPIO5, 5V_Relay.pin_3
  N5: U1.GPIO21, LCD.SDA
  N6: U1.GPIO22, LCD.SCL
  N7: 5V_Relay.pin_4, Water_Pump.pin_1
  N8: +5V_Power_Supply.pin1, Switch.leg1

custom parts:
  ESP32-38PinWide: Generic 38-Pin ESP32 with wide format (only access to one side of pins on a breadboard) based on Stephen Lilley's HiLetgo ESP-WROOM-32 ESP32 ESP-32S Development Board.
  LCD1602-I2C: A standard character display, usually with 2x16 characters. Comes in many colors with LCM1602 IIC attached.
  1 chan 5v relay module: 1 Channel 5V Relay Module Board Shield with Optocoupler Support High and Low Level Trigger for Arduino.
  Humidity and Temperature Sensor DHT11: Digital relative humidity & temperature sensor DHT11
  Water Level Sensor: A water level sensor. This sensor operates at 3V to 5V. The Sig (signal) pin outputs an analogue signal that is in proportion to the amount of water in contact with the sensor.
