# Fritzing sketch Taiwo2 (saved by Fritzing 0.9.3b)

parts:
  U1 = ESP32-38PinWide [part_number=ESP32-38PinWide]
  LCD = LCD1602-I2C
  Soil_Moisture = Soil Moisture Sensor
  DHT11 = Humidity and Temperature Sensor DHT11
  +5V_Power_Supply = Camdenboss CTB0158-2 [part_number=CTB0158-2 package=THT]
  Water_Pump = DC Motor
  Switch = Square Pushbutton
  Q1 = NPN-Transistor [package="TO92 [THT]"]
  R1 = Resistor [tolerance=±5% resistance=220 package=THT]
  +5V_Power_Supply2 = Camdenboss CTB0158-2 [part_number=CTB0158-2 package=THT]

nets:
  N1: U1.GPIO35, Soil_Moisture.SIG
  GND: U1.GND, LCD.GND, Soil_Moisture.GND, DHT11.GND_2, +5V_Power_Supply.pin2, Water_Pump.pin_2, +5V_Power_Supply2.pin2
  5V: U1.VIN, LCD.VCC, Soil_Moisture.VCC, DHT11.Vcc, Switch.leg0
  N2: U1.GPIO4, R1.Pin_0
  N3: U1.GPIO5, DHT11.Data-signal
  N4: U1.GPIO21, LCD.SDA
  N5: U1.GPIO22, LCD.SCL
  N6: +5V_Power_Supply.pin1, Switch.leg1
  N7: Water_Pump.pin_1, Q1.E
  N8: Q1.B, R1.Pin_1
  N9: Q1.C, +5V_Power_Supply2.pin1

custom parts:
  ESP32-38PinWide: Generic 38-Pin ESP32 with wide format (only access to one side of pins on a breadboard) based on Stephen Lilley's HiLetgo ESP-WROOM-32 ESP32 ESP-32S Development Board.
  LCD1602-I2C: A standard character display, usually with 2x16 characters. Comes in many colors with LCM1602 IIC attached.
  Humidity and Temperature Sensor DHT11: Digital relative humidity & temperature sensor DHT11
