# Fritzing sketch Treasure (saved by Fritzing 0.9.3b)

parts:
  U1 = ESP32-38PinWide [part_number=ESP32-38PinWide]
  Part1 = LCD1602-I2C
  HC-SR04_Sensor_1 = HC-SR04 Ultrasonic Distance Sensor
  J1 = Screw terminal - 2 pins [package=THT]
  5V_Relay = RELAY [package=relay-g5q]
  BC547 = TRANSISTOR_NPN [package=to-92-ammo]
  R1 = Resistor [tolerance=±5% resistance=220 package="0402 [SMD]"]
  5V_Power_Supply = Power plug
  Pumping_Machine_Connector = Camdenboss CTB0158-2 [part_number=CTB0158-2 package=THT]

nets:
  N1: U1.GPIO14, R1.Pin_1
  GND: U1.GND, Part1.GND, HC-SR04_Sensor_1.ECHO, J1.pin2, BC547.E, 5V_Power_Supply.GND
  VIN: U1.VIN, HC-SR04_Sensor_1.VCC
  N2: U1.GPIO5, HC-SR04_Sensor_1.TRIG
  N3: U1.GPIO18, HC-SR04_Sensor_1.GND
  N4: U1.GPIO21, Part1.SDA
  N5: U1.GPIO22, Part1.SCL
  VCC: Part1.VCC, J1.pin1, 5V_Relay.COIL1, 5V_Power_Supply.VCC
  N6: 5V_Relay.COIL2, BC547.C
  N7: 5V_Relay.MAIN, Pumping_Machine_Connector.pin1
  N8: 5V_Relay.NO, Pumping_Machine_Connector.pin2
  N9: BC547.B, R1.Pin_0

custom parts:
  ESP32-38PinWide: Generic 38-Pin ESP32 with wide format (only access to one side of pins on a breadboard) based on Stephen Lilley's HiLetgo ESP-WROOM-32 ESP32 ESP-32S Development Board.
  LCD1602-I2C: A standard character display, usually with 2x16 characters. Comes in many colors with LCM1602 IIC attached.
