# Fritzing sketch audiopcb (saved by Fritzing 0.9.3b)

parts:
  Q1 = BD140 [part_number=MJE350 package="TO-126 [THT]"]
  Q3 = PNP-Transistor [part_number=2N5401 package="TO92 [THT]"]
  Q2 = NPN-Transistor [part_number=MJE340 package="TO92 [THT]"]
  Q4 = NPN-Transistor [part_number=2N5551 package="TO92 [THT]"]
  Q5 = pnp-Powertransistor [part_number="2SA1837 " package="TO220 [THT]"]
  Q6 = npn-Powertransistor [part_number=2SC4793 package="TO220 [THT]"]
  Q7 = npn-Powertransistor [part_number=2SC5198 package="TO220 [THT]"]
  Q8 = pnp-Powertransistor [part_number=2SA1941 package="TO220 [THT]"]
  Q9 = npn-Powertransistor [part_number=2SC5200 package="TO220 [THT]"]
  D1 = Diode [part_number=1N4007 package=diode-hv]
  D2 = Diode [part_number=1N4007 package=diode-hv]
  R1 = TRIMPOT [part_number=200 package=trim_pot_pth]
  R2 = Resistor [tolerance=±5% resistance=390 package=THT]
  R3 = Resistor [tolerance=±5% resistance=56k package=THT]
  R4 = Resistor [tolerance=±5% resistance=4.7k package=THT]
  R5 = Resistor [tolerance=±5% resistance=2.7k package=THT]
  R6 = Resistor [tolerance=±5% resistance=10 package=THT]
  R7 = Resistor [tolerance=±5% resistance=56k package=THT]
  R8 = Resistor [tolerance=±5% resistance=470 package=THT]
  R9 = Resistor [tolerance=±5% resistance=5.6k package=THT]
  R10 = Resistor [tolerance=±5% resistance=10k package=THT]
  Q10 = NPN-Transistor [part_number=2N5551 package="TO92 [THT]"]
  D3 = Diode [part_number=1N4007 package=diode-hv]
  D4 = Diode [part_number=1N4007 package=diode-hv]
  C1 = Ceramic Capacitor [capacitance="100 nF" package="0603 [SMD, multilayer]"]
  Q11 = PNP-Transistor [part_number=2N5401 package="TO92 [THT]"]
  R11 = Resistor [tolerance=±5% resistance=10 package=THT]
  R12 = Resistor [tolerance=±5% resistance=4.7k package=THT]
  R13 = Resistor [tolerance=±5% resistance=2.7k package=THT]
  R14 = Resistor [tolerance=±5% resistance=220 package=THT]
  R16 = Resistor [tolerance=±5% resistance=220 package=THT]
  R17 = Resistor [tolerance=±5% resistance=10k package=THT]
  R18 = Resistor [tolerance=±5% resistance=33k package=THT]
  R19 = Resistor [tolerance=±5% resistance=330 package=THT]
  Q12 = NPN-Transistor [part_number=MJE340 package="TO92 [THT]"]
  R20 = Resistor [tolerance=±5% resistance=1k package=THT]
  R21 = TRIMPOT [part_number=1k package=trim_pot_pth]
  R22 = Resistor [tolerance=±5% resistance=390 package=THT]
  R23 = Resistor [tolerance=±5% resistance=330 package=THT]
  Q13 = pnp-Powertransistor [part_number=2SA1941 package="TO220 [THT]"]
  R24 = Resistor [tolerance=±5% resistance=150 power=2W package=THT]
  R15 = Resistor [tolerance=±5% resistance=100 package=THT]
  Q14 = npn-Powertransistor [part_number=2SC5198 package="TO220 [THT]"]
  R25 = Resistor [tolerance=±5% resistance=150 package=THT]
  R26 = Resistor [tolerance=±5% resistance=150 package=THT]
  R27 = Resistor [tolerance=±5% resistance=150 package=THT]
  Q15 = pnp-Powertransistor [part_number=2SA1943 package="TO220 [THT]"]
  +B = male pin header, 1 pin [form="♂ (male)"]
  FB = male pin header, 1 pin [form="♂ (male)"]
  -B = male pin header, 1 pin [form="♂ (male)"]
  +120V = male pin header, 1 pin [form="♂ (male)"]
  -120V = male pin header, 1 pin [form="♂ (male)"]
  J2 = Camdenboss CTB0158-2 [part_number=INPUT package=THT]
  C8 = Electrolytic Capacitor [part_number=100uF package="2cm H-Type"]
  C9 = Electrolytic Capacitor [part_number=470uF package="2cm H-Type"]
  C10 = Electrolytic Capacitor [part_number=220uF package="2cm H-Type"]
  C11 = Capacitor [part_number=33nF package=cap-pth-small-kit]
  C12 = Electrolytic Capacitor [part_number=10uF package="2cm H-Type"]

nets:
  N1: Q1.emitter, R1.CCW
  N2: Q1.collector, R11.Pin_0
  N3: Q1.base, D1.C, R3.Pin_1
  N4: Q3.E, Q11.E, R11.Pin_1
  N5: Q3.B, Q4.B, R10.Pin_1, C1.1
  N6: Q3.C, Q6.base, R12.Pin_0
  N7: Q2.E, R8.Pin_0
  N8: Q2.B, R7.Pin_1, D4.A
  N9: Q2.C, R6.Pin_1
  N10: Q4.E, R6.Pin_0, Q10.E
  N11: Q4.C, Q5.base, R4.Pin_1
  N12: Q5.collector, Q7.base, Q12.C
  N13: Q5.emitter, R19.Pin_1
  N14: Q6.collector, Q8.base, Q12.E, R21.CCW, R21.WIPER, C12.-
  N15: Q6.emitter, R22.Pin_1
  N16: Q7.collector, Q9.collector, D2.A, R2.Pin_0, R4.Pin_0, R5.Pin_0, R19.Pin_0, Q14.collector, +120V.pin1
  N17: Q7.emitter, R23.Pin_1, Q14.base, R25.Pin_0
  N18: Q8.collector, R8.Pin_1, D3.C, R12.Pin_1, R13.Pin_1, R22.Pin_0, Q13.collector, Q15.collector, -120V.pin1
  N19: Q8.emitter, R23.Pin_0, Q13.base, R24.Pin_0
  N20: Q9.base, Q14.emitter, R25.Pin_1
  N21: Q9.emitter, R26.Pin_0, +B.pin1
  N22: D1.A, D2.C
  N23: R1.WIPER, R1.CW, R2.Pin_1
  GND: R3.Pin_0, R7.Pin_0, R10.Pin_0, J2.pin2, C8.-, C9.-, C10.-
  N24: R5.Pin_1, Q10.C
  N25: R9.Pin_0, J2.pin1
  N26: R9.Pin_1, C1.0
  N27: Q10.B, Q11.B, R14.Pin_1, R16.Pin_0, R15.Pin_1, C11.2
  N28: D3.A, D4.C
  N29: Q11.C, R13.Pin_0
  N30: R14.Pin_0, C8.+
  N31: R16.Pin_1, C10.+
  N32: R17.Pin_1, R18.Pin_1
  N33: R18.Pin_0, C11.1
  N34: Q12.B, R20.Pin_0, R21.CW
  N35: R20.Pin_1, C12.+
  N36: Q13.emitter, R24.Pin_1, Q15.base
  N37: R15.Pin_0, C9.+
  N38: R26.Pin_1, R27.Pin_0, FB.pin1
  N39: R27.Pin_1, Q15.emitter, -B.pin1
  N40: J2.terminal_1, J2.terminal_2

custom parts:
  BD140: A pnp transistor which can drive a higher load
