# Fritzing sketch bj (saved by Fritzing 0.9.3b)

parts:
  R1 = Resistor [tolerance=±5% resistance=220 package=THT]
  U1 = ESP32-38PinWide [part_number=ESP32-38PinWide]
  LCD = LCD1602-I2C
  U3 = RELAY [part_number="40A Relay" package=relay-t9a-2]
  Q1 = TRANSISTOR_NPN [part_number=BC547 package=to-92]
  GSM_Module = SIM800L [package=THT]
  M1 = Pzem-004t [part_number="Voltage-Current Sensor"]
  part = Camdenboss CTB0158-2 [part_number="Socket Terminal" package=THT]
  D1 = Diode [part_number=1N4007 package=diode-hv]
  part_2 = Camdenboss CTB0158-2 [part_number="220V AC Source" package=THT]
  220V_AC_-_12V_AC_Transformer = bridge rectifier TO-269AA [package="TO-269AA [SMD]"]
  U4 = Transformer [package=transformer]
  C1 = Tantalum Capacitor [capacitance=104pF package="B 3528 [SMD, tantalum]"]
  C2 = Electrolytic Capacitor [capacitance=1000µF package="300 mil [THT, electrolytic]"]  # not connected
  L7805 = Voltage Regulator [package=78xxl]
  100uF = Capacitor Polarized [package=cpol-radial-1000uf-63v]

nets:
  N1: R1.Pin_0, U1.GPIO17
  N2: R1.Pin_1, Q1.B
  GND: U1.GND, LCD.GND, Q1.E, M1.GND, 220V_AC_-_12V_AC_Transformer.DC-, C1.-, L7805.GND, 100uF.-
  VIN: U1.VIN, LCD.VCC, U3.COIL1, M1.5V, D1.C, L7805.OUT, 100uF.+
  N3: U1.GPIO18, GSM_Module.SIM_RXD
  N4: U1.GPIO19, GSM_Module.SIM_TXD
  N5: U1.GPIO21, LCD.SDA
  N6: U1.GPIO3, M1.TX
  N7: U1.GPIO1, M1.RX
  N8: U1.GPIO22, LCD.SCL
  N9: U3.COIL2, Q1.C, D1.A
  N10: U3.MAIN, part_2.pin1
  N11: U3.NC, part.pin1
  N12: part.pin2, part_2.pin2
  N13: 220V_AC_-_12V_AC_Transformer.AC#0, U4.3
  N14: 220V_AC_-_12V_AC_Transformer.AC#1, U4.4
  N15: 220V_AC_-_12V_AC_Transformer.DC+, C1.+, L7805.IN

notes:
  Power Supply
  Microcontroller & Sensors

custom parts:
  ESP32-38PinWide: Generic 38-Pin ESP32 with wide format (only access to one side of pins on a breadboard) based on Stephen Lilley's HiLetgo ESP-WROOM-32 ESP32 ESP-32S Development Board.
  LCD1602-I2C: A standard character display, usually with 2x16 characters. Comes in many colors with LCM1602 IIC attached.
  Pzem-004t: Pzem-004t used for measuring AC voltage, current, active power, frequency, power factor and active energy, the module is without display function, the data is read through the TTL interface.
