# Fritzing sketch inventory_proj (saved by Fritzing 0.9.3b)

parts:
  U1 = ESP32-38PinWide [part_number=ESP32-38PinWide]
  Part1 = HX711 Weighing Sensor Module
  Bathroom_scale_load_cell = Load Sensor - 50kg [part_number=SEN-10245]
  Bathroom_Scale_Load_Cells = Load Sensor - 50kg [part_number=SEN-10245]
  Bathroom_scale_load_cell_2 = Load Sensor - 50kg [part_number=SEN-10245]
  Bathroom_scale_load_cell_3 = Load Sensor - 50kg [part_number=SEN-10245]
  LCD = LCD1602-I2C
  R1 = Resistor [tolerance=±5% resistance=220 package="0805 [SMD]"]
  S5 = SWITCH-MOMENTARY-2 [package=tactile-pth-12mm]
  220V_AC_-_12V_AC_Transformer1 = bridge rectifier TO-269AA [package="TO-269AA [SMD]"]
  U5 = Transformer [package=transformer]
  C3 = Tantalum Capacitor [capacitance=104pF package="B 3528 [SMD, tantalum]"]
  C4 = Electrolytic Capacitor [capacitance=1000µF package="300 mil [THT, electrolytic]"]  # not connected
  L7805 = Voltage Regulator [package=78xxl]
  100uF1 = Capacitor Polarized [package=cpol-radial-1000uf-63v]
  J3 = Camdenboss CTB0158-2 [part_number="220V AC Source" package=THT]

nets:
  N1: U1.GPIO27, Part1.DO/RX
  N2: U1.GPIO14, Part1.CK/TX
  VCC: U1.VIN, Part1.VCC, LCD.VCC, R1.Pin_0, L7805.OUT
  N3: U1.GPIO21, LCD.SDA
  N4: U1.GPIO22, LCD.SCL
  GND: U1.GND, Part1.GND, LCD.GND, S5.2, 220V_AC_-_12V_AC_Transformer1.DC-, C3.-, L7805.GND, 100uF1.-
  N5: Part1.E+, Bathroom_Scale_Load_Cells.R
  N6: Part1.E-, Bathroom_scale_load_cell_3.R
  N7: Part1.A+, Bathroom_scale_load_cell_2.R
  N8: Part1.A-, Bathroom_scale_load_cell.R
  N9: Bathroom_scale_load_cell.B, Bathroom_Scale_Load_Cells.B
  N10: Bathroom_scale_load_cell.W, Bathroom_scale_load_cell_3.W
  N11: Bathroom_Scale_Load_Cells.W, Bathroom_scale_load_cell_2.W
  N12: Bathroom_scale_load_cell_2.B, Bathroom_scale_load_cell_3.B
  N13: R1.Pin_1, S5.1
  N14: 220V_AC_-_12V_AC_Transformer1.AC#0, U5.3
  N15: 220V_AC_-_12V_AC_Transformer1.AC#1, U5.4
  N16: 220V_AC_-_12V_AC_Transformer1.DC+, C3.+, L7805.IN
  N17: U5.1, J3.pin2
  N18: U5.2, J3.pin1

custom parts:
  ESP32-38PinWide: Generic 38-Pin ESP32 with wide format (only access to one side of pins on a breadboard) based on Stephen Lilley's HiLetgo ESP-WROOM-32 ESP32 ESP-32S Development Board.
  Load Sensor - 50kg: Half-wheatstone bridge Load Cell modified from the Fritzing Repo This load sensor, sometimes called a strain gauge, is the same one found in digital bathroom scales (you know, the ones you use in January for your New Year's resolutions, and then forget about a month later). This sensor can measure up to about 110 pounds.
  LCD1602-I2C: A standard character display, usually with 2x16 characters. Comes in many colors with LCM1602 IIC attached.
