# Fritzing sketch m_w_project (saved by Fritzing 0.9.3b)

parts:
  Part1 = Arduino Uno (Rev3)
  J1 = Piezo Speaker
  Part2 = Bluetooth HC-05 Macho
  Part3 = LCD1602-I2C
  DHT1 = Humidity and Temperature Sensor DHT11
  U1 = GAS_SENSOR [package=mq-3]
  YF-S201_Flow_Meter2 = YF-S201 Water Flow Meter
  J2 = Screw terminal - 2 pins [package=THT]
  Q1 = NPN-Transistor [package="TO92 [THT]"]  # not connected
  R1 = Resistor [tolerance=±5% resistance=220 package="0603 [SMD]"]

nets:
  N1: Part1.A3, U1.A1
  N2: Part1.A4/SDA, Part3.SDA
  N3: Part1.A5/SCL, Part3.SCL
  N4: Part1.D10_PWM/SS, Part2.RXD
  N5: Part1.D11_PWM/MOSI, Part2.TXD
  N6: Part1.D13/SCK, R1.Pin_0
  N7: Part1.D2, YF-S201_Flow_Meter2.SIG
  N8: Part1.D5_PWM, DHT1.Data-signal
  N9: Part1.VIN, J2.pin2
  N10: J1.pin2, DHT1.Vcc

notes:
  DHT11
  Water Flow Rate
  MQ2
  Turbidity Sensor
  LCD
  Buzzer
  BC547
  Arduino Uno
  +7.4V
  +5V
  GND

custom parts:
  LCD1602-I2C: A standard character display, usually with 2x16 characters. Comes in many colors with LCM1602 IIC attached.
  Humidity and Temperature Sensor DHT11: Digital relative humidity & temperature sensor DHT11
  YF-S201 Water Flow Meter: The YF-S201 Flow Meter. The input voltage is 5V to 24V (DC).
