# Fritzing sketch mcansat (saved by Fritzing 0.9.3b)
circuit board: 10.2766cm x 8.15677cm

parts:
  Pico/Pico2_Mod_1 = Raspberry Pi Pico or Pico 2
  NRF24L01 = female pin header, 4 pins [form="♀ (female)"]
  part = female pin header, 4 pins [form="♀ (female)"]
  MOD1 = MT3608 Boost No usb
  BME280 = female pin header, 4 pins [form="♀ (female)"]
  MQ7 = female pin header, 4 pins [form="♀ (female)"]
  SERVO = male alternating pin header, 3 pins [form="♂ (male)"]
  S1 = Toggle Switch [package=THT]
  J1 = Camdenboss CTB0158-2 [part_number=CTB0158-2 package=THT]

nets:
  N1: Pico/Pico2_Mod_1.pin_3, Pico/Pico2_Mod_1.pin_18, Pico/Pico2_Mod_1.pin_23, Pico/Pico2_Mod_1.pin_38, part.pin4, MOD1.IN_(-), MOD1.OUT_(-), BME280.pin2, MQ7.pin3, SERVO.pin3, J1.pin2
  N2: Pico/Pico2_Mod_1.pin_4, SERVO.pin1
  N3: Pico/Pico2_Mod_1.pin_6, part.pin1
  N4: Pico/Pico2_Mod_1.pin_9, part.pin2
  N5: Pico/Pico2_Mod_1.pin_10, NRF24L01.pin2
  N6: Pico/Pico2_Mod_1.pin_19, part.pin3
  N7: Pico/Pico2_Mod_1.pin_20, NRF24L01.pin3
  N8: Pico/Pico2_Mod_1.pin_26, BME280.pin4
  N9: Pico/Pico2_Mod_1.pin_27, BME280.pin3
  N10: Pico/Pico2_Mod_1.pin_31, MQ7.pin1
  N11: Pico/Pico2_Mod_1.pin_36, NRF24L01.pin4, BME280.pin1, MQ7.pin4
  N12: Pico/Pico2_Mod_1.pin_39, MOD1.OUT_(+), SERVO.pin2
  N13: MOD1.IN_(+), S1.L1
  N14: S1.COM, J1.pin1

notes:
  CanSat FUTA

custom parts:
  Raspberry Pi Pico or Pico 2: Raspberry Pi Pico and Pico 2. Based around the RP2040 and RP2350 microcontrollers respectively, Picos are low cost microcontroller device bringing Raspberry Pi quality, cost, and easy of use to the microcontroller space. Jan 2021, Split part in to two versions: tht (this one) and SMD. This one will drill holes for a .1 in header in pcb to allow plugging in the module as well as providing pads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
  MT3608 Boost No usb: Chip- MT3608 / B6289 DC to DC step up, power booster module. With adjustable output voltage. Current- 2A . || Input voltage- 2V-24V || Output voltage- 5V-28V Input interface- Inversed polarity- NO. || Led indicator- No.
