# Fritzing sketch power supply (saved by Fritzing 0.9.3b)
circuit board: 12.7659cm x 2.61525cm

parts:
  IC1 = Voltage Regulator [package=to-220-alt]
  J1 = Camdenboss CTB0158-2 [part_number=CTB0158-2 package=THT]
  J2 = Camdenboss CTB0158-2 [part_number=CTB0158-2 package=THT]
  C3 = Capacitor Polarized [package=cpol-radial-10uf-25v]
  U1 = Transformer [package=transformer]
  C2 = Electrolytic Capacitor [capacitance=1000µF package="100 mil [THT, electrolytic]"]
  LED1 = LED - 3mm [color="Red (633nm)" package="3 mm [THT]"]
  C1 = Ceramic Capacitor [capacitance="100 nF" package="200 mil [THT, multilayer]"]
  R1 = Resistor [tolerance=±5% resistance=220 package=THT]
  D1 = bridge rectifier round [package="round [THT]"]

nets:
  N1: IC1.GND, J1.pin2, C3.-, C2.-, LED1.cathode, C1.0, D1.DC-
  N2: IC1.IN, C2.+, C1.1, D1.DC+
  N3: IC1.OUT, J1.pin1, C3.+, R1.Pin_0
  N4: J2.pin1, U1.1
  N5: J2.pin2, U1.2
  N6: U1.3, D1.AC#0
  N7: U1.4, D1.AC#1
  N8: LED1.anode, R1.Pin_1
